# Fritzing sketch Midterm-2-Fritzing (saved by Fritzing 0.9.9b)
breadboards: 1

parts:
  Argon1 = Particle Argon  # not connected
  OLED_I2C1 = OLED 128x64 I2C Monochrome Display  # not connected
  SENS1 = SoilWatch 10  # not connected
  M1 = BMP280  # not connected
  Relay1 = Relay - 6 pins [package="DIP (Dual Inline) [THT]"]  # not connected
  M2 = DC Motor  # not connected
  Q1 = PNP-Transistor [package="TO92 [THT]"]
  R1 = Resistor [tolerance=±5% resistance=220 package="0402 [SMD]"]  # not connected
  R2 = Resistor [tolerance=±5% resistance=220 package="2010 [SMD]"]

nets:
  N1: Q1.B, R2.Pin_0

custom parts:
  Particle Argon: The Argon is a powerful Wi-Fi enabled development board that can act as either a standalone Wi-Fi endpoint or Wi-Fi enabled gateway for Particle Mesh networks. It is based on the Nordic nRF52840 and has built-in battery charging circuitry so it’s easy to connect a Li-Po and deploy your local network in minutes. The Argon is great for connecting existing projects to the Particle Device Cloud or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
  SoilWatch 10: SoilWatch 10 - Capacitive soil moisture sensor
  BMP280: Temperature Humidity Barometric presure Sensor, I2C
  Relay - 6 pins: A DIP stand-in part for whatever IC you want. With 6 pins on a 900mil dual inline package (DIP) footprint.
